# Fritzing sketch LaserReceiver (saved by Fritzing 0.8.5b)
circuit board: 4.19661cm x 3.0568cm
breadboards: 1

parts:
  U1 = LM 358 Dual Op-Amp [package="DIP8 [THT]"]
  R1 = Resistor [tolerance=±5% resistance=4.7k package=THT]
  R3 = Resistor [tolerance=±5% resistance=1M package=THT]
  J1(Rx) = female pin header, 1 pin [form="♀ (female)"]
  R2 = Resistor [tolerance=±5% resistance=330k package=THT]
  P1 = S1133 Si Photodiode [package="8mm Ceramic [THT]"]

nets:
  N1: U1.connector0, J1(Rx).pin1, R2.Pin_1
  N2: U1.connector1, R1.Pin_1, R2.Pin_0
  GND: U1.connector2, U1.connector3, P1.anode
  5V: U1.connector7, R3.Pin_1
  N3: R1.Pin_0, R3.Pin_0, P1.cathode
