# Fritzing sketch LaserTransmitter (saved by Fritzing 0.8.5b)
circuit board: 3.03702cm x 3.24405cm
breadboards: 1

parts:
  J1_(Tx) = female pin header, 1 pin [form="♀ (female)"]
  Q1 = Basic FET N-Channel [package="TO220 [THT]"]
  R1 = Resistor [tolerance=±5% resistance=2.2k package=THT]
  LED1_(LASER) = LED - 5mm [color="Red (635nm)" package="5 mm [THT]"]
  R2 = Resistor [tolerance=±5% resistance=100 package=THT]

nets:
  N1: J1_(Tx).pin1, Q1.gate, R1.Pin_0
  N2: Q1.drain, LED1_(LASER).cathode
  GND: Q1.source, R1.Pin_1
  N3: LED1_(LASER).anode, R2.Pin_1
  5V: R2.Pin_0
